// Logisim project monociclo.circ as structural Verilog: 6 circuits, main circuit main
module main (
);

  wire ALUsrc, button_1_out, CLK, MEM_READ, MEM_WRITE, MemToReg, PCsrc, RegWrite, Zero;
  wire [1:0] ALUop, INST_TYPE;
  wire [2:0] FUNCT3;
  wire [4:0] RD;
  wire [6:0] FUNCT7, OPCODE;
  wire [23:0] adder_1_out, adder_2_out, imm_gen_1_imediato, multiplexer_1_out, PC_q;
  wire [24:15] MEMORIA_DE_INSTRUCOES_data;
  wire [31:0] alu_1_aluresult, banco_regs_1_read_data1, banco_regs_1_read_data2, MEMORIA_DE_DADOS_dout,
       multiplexer_2_out, multiplexer_3_out;
  wire [31:24] imm_gen_1_imediato_2;

  Clock clock_1 (.out(CLK));
  Register #(.width(24)) PC (.D(multiplexer_1_out), .en(1'b1), .clk(CLK), .Q(PC_q), .clr(button_1_out));
  Multiplexer #(.width(24)) multiplexer_1 (.in0(adder_1_out), .in1(adder_2_out), .out(multiplexer_1_out), .sel(PCsrc));
  Adder #(.width(24)) adder_1 (.a(24'h1), .b(PC_q), .out(adder_1_out));  // open: cin, cout
  Button button_1 (.out(button_1_out));
  ROM #(.addrWidth(24), .dataWidth(32)) MEMORIA_DE_INSTRUCOES (
    .addr(PC_q), .data({FUNCT7, MEMORIA_DE_INSTRUCOES_data, FUNCT3, RD, OPCODE}));
  banco_regs banco_regs_1 (
    .Write_Enable(RegWrite), .CLOCK(CLK), .Read_Registrador2(MEMORIA_DE_INSTRUCOES_data[24:20]),
    .Read_Registrador1(MEMORIA_DE_INSTRUCOES_data[19:15]), .Write_Data(multiplexer_3_out),
    .Write_Registrador(RD), .Read_Data1(banco_regs_1_read_data1), .Read_Data2(banco_regs_1_read_data2));
  imm_gen imm_gen_1 (
    .Imm_Bits({FUNCT7, MEMORIA_DE_INSTRUCOES_data, FUNCT3, RD, OPCODE}), .INST_TYPE(INST_TYPE),
    .Imediato({imm_gen_1_imediato_2, imm_gen_1_imediato}));
  ALU alu_1 (
    .A(banco_regs_1_read_data1), .B(multiplexer_2_out), .ALUoperation(ALUop), .Zero(Zero),
    .ALUresult(alu_1_aluresult));
  Multiplexer #(.width(32)) multiplexer_2 (
    .in0(banco_regs_1_read_data2), .in1({imm_gen_1_imediato_2, imm_gen_1_imediato}), .out(multiplexer_2_out),
    .sel(ALUsrc));
  Adder #(.width(24)) adder_2 (.a(PC_q), .b(imm_gen_1_imediato), .out(adder_2_out));  // open: cin, cout
  RAM #(.addrWidth(24), .dataWidth(32)) MEMORIA_DE_DADOS (
    .addr(alu_1_aluresult[23:0]), .we(MEM_WRITE), .oe(MEM_READ), .clk(CLK), .din(banco_regs_1_read_data2),
    .dout(MEMORIA_DE_DADOS_dout));
  Multiplexer #(.width(32)) multiplexer_3 (
    .in0(alu_1_aluresult), .in1(MEMORIA_DE_DADOS_dout), .out(multiplexer_3_out), .sel(MemToReg));

  // Notes on the sheet:
  //   CONTROLE
  //   contents of MEMORIA_DE_INSTRUCOES (hex, n*v repeats v):
  //   1000b3 40100133 20a5a3 208563
  //   ADRESS_MEM
  //   MEM_DATA
  //   ALU_RESULT
endmodule

module banco_regs (
  input  Write_Enable,
  input  CLOCK,
  input  [31:0] Write_Data,
  input  [4:0] Write_Registrador,
  input  [4:0] Read_Registrador1,
  input  [4:0] Read_Registrador2,
  output [31:0] Read_Data1,
  output [31:0] Read_Data2
);

  wire [31:0] demultiplexer_1_out1, demultiplexer_1_out2, demultiplexer_1_out3, demultiplexer_1_out4,
       demultiplexer_1_out5, demultiplexer_1_out6, demultiplexer_1_out7, demultiplexer_1_out8,
       demultiplexer_1_out9, demultiplexer_1_out10, demultiplexer_1_out11, demultiplexer_1_out12,
       demultiplexer_1_out13, demultiplexer_1_out14, demultiplexer_1_out15, demultiplexer_1_out16,
       demultiplexer_1_out17, demultiplexer_1_out18, demultiplexer_1_out19, demultiplexer_1_out20,
       demultiplexer_1_out21, demultiplexer_1_out22, demultiplexer_1_out23, demultiplexer_1_out24,
       demultiplexer_1_out25, demultiplexer_1_out26, demultiplexer_1_out27, demultiplexer_1_out28,
       demultiplexer_1_out29, demultiplexer_1_out30, demultiplexer_1_out31, x0, x1, x2, x3, x4, x5, x6, x7,
       x8, x9, x10, x11, x12, x13, x14, x15, x16, x17, x18, x19, x20, x21, x22, x23, x24, x25, x26, x27, x28,
       x29, x30, x31;

  Demultiplexer #(.select(5), .width(32)) demultiplexer_1 (
    .out1(demultiplexer_1_out1), .out2(demultiplexer_1_out2), .out3(demultiplexer_1_out3),
    .out4(demultiplexer_1_out4), .out5(demultiplexer_1_out5), .out6(demultiplexer_1_out6),
    .out7(demultiplexer_1_out7), .out8(demultiplexer_1_out8), .out9(demultiplexer_1_out9),
    .out10(demultiplexer_1_out10), .out11(demultiplexer_1_out11), .out12(demultiplexer_1_out12),
    .out13(demultiplexer_1_out13), .out14(demultiplexer_1_out14), .out15(demultiplexer_1_out15),
    .out16(demultiplexer_1_out16), .out17(demultiplexer_1_out17), .out18(demultiplexer_1_out18),
    .out19(demultiplexer_1_out19), .out20(demultiplexer_1_out20), .out21(demultiplexer_1_out21),
    .out22(demultiplexer_1_out22), .out23(demultiplexer_1_out23), .out24(demultiplexer_1_out24),
    .out25(demultiplexer_1_out25), .out26(demultiplexer_1_out26), .out27(demultiplexer_1_out27),
    .out28(demultiplexer_1_out28), .out29(demultiplexer_1_out29), .out30(demultiplexer_1_out30),
    .out31(demultiplexer_1_out31), .in(Write_Data), .sel(Write_Registrador));  // open: out0
  Register #(.width(32)) register_1 (.D({32{1'b0}}), .en(Write_Enable), .clk(CLOCK), .Q(x0));  // open: clr
  Register #(.width(32)) register_2 (.D(demultiplexer_1_out1), .en(Write_Enable), .clk(CLOCK), .Q(x1));  // open: clr
  Register #(.width(32)) register_3 (.D(demultiplexer_1_out2), .en(Write_Enable), .clk(CLOCK), .Q(x2));  // open: clr
  Register #(.width(32)) register_4 (.D(demultiplexer_1_out3), .en(Write_Enable), .clk(CLOCK), .Q(x3));  // open: clr
  Register #(.width(32)) register_5 (.D(demultiplexer_1_out4), .en(Write_Enable), .clk(CLOCK), .Q(x4));  // open: clr
  Register #(.width(32)) register_6 (.D(demultiplexer_1_out5), .en(Write_Enable), .clk(CLOCK), .Q(x5));  // open: clr
  Register #(.width(32)) register_7 (.D(demultiplexer_1_out6), .en(Write_Enable), .clk(CLOCK), .Q(x6));  // open: clr
  Register #(.width(32)) register_8 (.D(demultiplexer_1_out7), .en(Write_Enable), .clk(CLOCK), .Q(x7));  // open: clr
  Register #(.width(32)) register_9 (.D(demultiplexer_1_out8), .en(Write_Enable), .clk(CLOCK), .Q(x8));  // open: clr
  Register #(.width(32)) register_10 (.D(demultiplexer_1_out9), .en(Write_Enable), .clk(CLOCK), .Q(x9));  // open: clr
  Register #(.width(32)) register_11 (.D(demultiplexer_1_out10), .en(Write_Enable), .clk(CLOCK), .Q(x10));  // open: clr
  Register #(.width(32)) register_12 (.D(demultiplexer_1_out11), .en(Write_Enable), .clk(CLOCK), .Q(x11));  // open: clr
  Register #(.width(32)) register_13 (.D(demultiplexer_1_out12), .en(Write_Enable), .clk(CLOCK), .Q(x12));  // open: clr
  Register #(.width(32)) register_14 (.D(demultiplexer_1_out13), .en(Write_Enable), .clk(CLOCK), .Q(x13));  // open: clr
  Register #(.width(32)) register_15 (.D(demultiplexer_1_out14), .en(Write_Enable), .clk(CLOCK), .Q(x14));  // open: clr
  Register #(.width(32)) register_16 (.D(demultiplexer_1_out15), .en(Write_Enable), .clk(CLOCK), .Q(x15));  // open: clr
  Register #(.width(32)) register_17 (.D(demultiplexer_1_out16), .en(Write_Enable), .clk(CLOCK), .Q(x16));  // open: clr
  Register #(.width(32)) register_18 (.D(demultiplexer_1_out17), .en(Write_Enable), .clk(CLOCK), .Q(x17));  // open: clr
  Register #(.width(32)) register_19 (.D(demultiplexer_1_out18), .en(Write_Enable), .clk(CLOCK), .Q(x18));  // open: clr
  Register #(.width(32)) register_20 (.D(demultiplexer_1_out19), .en(Write_Enable), .clk(CLOCK), .Q(x19));  // open: clr
  Register #(.width(32)) register_21 (.D(demultiplexer_1_out20), .en(Write_Enable), .clk(CLOCK), .Q(x20));  // open: clr
  Register #(.width(32)) register_22 (.D(demultiplexer_1_out21), .en(Write_Enable), .clk(CLOCK), .Q(x21));  // open: clr
  Register #(.width(32)) register_23 (.D(demultiplexer_1_out22), .en(Write_Enable), .clk(CLOCK), .Q(x22));  // open: clr
  Register #(.width(32)) register_24 (.D(demultiplexer_1_out23), .en(Write_Enable), .clk(CLOCK), .Q(x23));  // open: clr
  Register #(.width(32)) register_25 (.D(demultiplexer_1_out24), .en(Write_Enable), .clk(CLOCK), .Q(x24));  // open: clr
  Register #(.width(32)) register_26 (.D(demultiplexer_1_out25), .en(Write_Enable), .clk(CLOCK), .Q(x25));  // open: clr
  Register #(.width(32)) register_27 (.D(demultiplexer_1_out26), .en(Write_Enable), .clk(CLOCK), .Q(x26));  // open: clr
  Register #(.width(32)) register_28 (.D(demultiplexer_1_out27), .en(Write_Enable), .clk(CLOCK), .Q(x27));  // open: clr
  Register #(.width(32)) register_29 (.D(demultiplexer_1_out28), .en(Write_Enable), .clk(CLOCK), .Q(x28));  // open: clr
  Register #(.width(32)) register_30 (.D(demultiplexer_1_out29), .en(Write_Enable), .clk(CLOCK), .Q(x29));  // open: clr
  Register #(.width(32)) register_31 (.D(demultiplexer_1_out30), .en(Write_Enable), .clk(CLOCK), .Q(x30));  // open: clr
  Register #(.width(32)) register_32 (.D(demultiplexer_1_out31), .en(Write_Enable), .clk(CLOCK), .Q(x31));  // open: clr
  Multiplexer #(.select(5), .width(32)) multiplexer_1 (
    .in0(x0), .in1(x1), .in2(x2), .in3(x3), .in4(x4), .in5(x5), .in6(x6), .in7(x7), .in8(x8), .in9(x9),
    .in10(x10), .in11(x11), .in12(x12), .in13(x13), .in14(x14), .in15(x15), .in16(x16), .in17(x17),
    .in18(x18), .in19(x19), .in20(x20), .in21(x21), .in22(x22), .in23(x23), .in24(x24), .in25(x25),
    .in26(x26), .in27(x27), .in28(x28), .in29(x29), .in30(x30), .in31(x31), .out(Read_Data1),
    .sel(Read_Registrador1));
  Multiplexer #(.select(5), .width(32)) multiplexer_2 (
    .in0(x0), .in1(x1), .in2(x2), .in3(x3), .in4(x4), .in5(x5), .in6(x6), .in7(x7), .in8(x8), .in9(x9),
    .in10(x10), .in11(x11), .in12(x12), .in13(x13), .in14(x14), .in15(x15), .in16(x16), .in17(x17),
    .in18(x18), .in19(x19), .in20(x20), .in21(x21), .in22(x22), .in23(x23), .in24(x24), .in25(x25),
    .in26(x26), .in27(x27), .in28(x28), .in29(x29), .in30(x30), .in31(x31), .out(Read_Data2),
    .sel(Read_Registrador2));

  // Other names for the same wires on the sheet: CLK = CLOCK; WE = Write_Enable
endmodule

module mem_instrucoes (
  input  pino_0,
  input  pino_1,
  input  pino_2,
  input  pino_3,
  input  pino_4,
  input  pino_5,
  input  pino_6,
  input  pino_7,
  input  pino_8,
  input  pino_9,
  input  pino_10,
  input  pino_11,
  input  pino_12,
  input  pino_13,
  input  pino_14,
  input  pino_15,
  input  [23:0] Mem_Endereco,
  input  pino_16,
  input  pino_17,
  input  pino_18,
  input  pino_19,
  input  pino_20,
  input  pino_21,
  input  pino_22,
  input  pino_23,
  input  pino_24,
  input  pino_25,
  input  pino_26,
  input  pino_27,
  input  pino_28,
  input  pino_29,
  input  pino_30,
  input  pino_31
);

  ROM #(.addrWidth(24)) MEM_0_7 (
    .addr(Mem_Endereco), .data({pino_7, pino_6, pino_5, pino_4, pino_3, pino_2, pino_1, pino_0}));
  ROM #(.addrWidth(24)) MEM_8_15 (
    .addr(Mem_Endereco), .data({pino_15, pino_14, pino_13, pino_12, pino_11, pino_10, pino_9, pino_8}));
  ROM #(.addrWidth(24)) MEM_16_23 (
    .addr(Mem_Endereco), .data({pino_23, pino_22, pino_21, pino_20, pino_19, pino_18, pino_17, pino_16}));
  ROM #(.addrWidth(24)) MEM_24_31 (
    .addr(Mem_Endereco), .data({pino_31, pino_30, pino_29, pino_28, pino_27, pino_26, pino_25, pino_24}));

  // Notes on the sheet:
  //   contents of MEM_0_7 (hex, n*v repeats v):
  //   f 33 5d dd 23 df 34 fd 32 da c ad aa 3d 39 66
  //   contents of MEM_8_15 (hex, n*v repeats v):
  //   f 33 5d dd 23 df 34 fd 32 da c ad aa 3d 39 66
  //   contents of MEM_16_23 (hex, n*v repeats v):
  //   f 33 5d dd 23 df 34 fd 32 da c ad aa 3d 39 66
  //   contents of MEM_24_31 (hex, n*v repeats v):
  //   f 33 5d dd 23 df 34 fd 32 da c ad aa 3d 39 66
endmodule

module ALU (
  input  [1:0] ALUoperation,
  input  [31:0] A,
  input  [31:0] B,
  output [31:0] ALUresult,
  output Zero
);

  wire not_1_out, not_2_out, not_3_out, not_4_out, not_5_out, not_6_out, not_7_out, not_8_out, not_9_out,
       not_10_out, not_11_out, not_12_out, not_13_out, not_14_out, not_15_out, not_16_out, not_17_out,
       not_18_out, not_19_out, not_20_out, not_21_out, not_22_out, not_23_out, not_24_out, not_25_out,
       not_26_out, not_27_out, not_28_out, not_29_out, not_30_out, not_31_out, not_32_out;
  wire [31:0] adder_1_out, and_1_out, or_1_out, subtractor_1_out;

  not not_1 (not_1_out, ALUresult[31]);
  not not_2 (not_2_out, ALUresult[30]);
  not not_3 (not_3_out, ALUresult[29]);
  not not_4 (not_4_out, ALUresult[28]);
  not not_5 (not_5_out, ALUresult[27]);
  Adder #(.width(32)) adder_1 (.a(A), .b(B), .out(adder_1_out));  // open: cin, cout
  Subtractor #(.width(32)) subtractor_1 (.a(A), .b(B), .out(subtractor_1_out));  // open: bin, bout
  assign and_1_out = A & B;  // AND_Gate and_1, 32 bits wide
  assign or_1_out = A | B;  // OR_Gate or_1, 32 bits wide
  not not_6 (not_6_out, ALUresult[26]);
  not not_7 (not_7_out, ALUresult[25]);
  not not_8 (not_8_out, ALUresult[24]);
  not not_9 (not_9_out, ALUresult[23]);
  not not_10 (not_10_out, ALUresult[22]);
  not not_11 (not_11_out, ALUresult[21]);
  not not_12 (not_12_out, ALUresult[20]);
  not not_13 (not_13_out, ALUresult[19]);
  Multiplexer #(.select(2), .width(32)) multiplexer_1 (
    .in0(adder_1_out), .in1(subtractor_1_out), .in2(and_1_out), .in3(or_1_out), .out(ALUresult),
    .sel(ALUoperation));
  not not_14 (not_14_out, ALUresult[18]);
  not not_15 (not_15_out, ALUresult[17]);
  not not_16 (not_16_out, ALUresult[16]);
  not not_17 (not_17_out, ALUresult[15]);
  and and_2 (Zero, not_1_out, not_2_out, not_3_out, not_4_out, not_5_out, not_6_out, not_7_out, not_8_out, not_9_out, not_10_out, not_11_out, not_12_out, not_13_out, not_14_out, not_15_out, not_16_out, not_17_out, not_18_out, not_19_out, not_20_out, not_21_out, not_22_out, not_23_out, not_24_out, not_25_out, not_26_out, not_27_out, not_28_out, not_29_out, not_30_out, not_31_out, not_32_out);
  not not_18 (not_18_out, ALUresult[14]);
  not not_19 (not_19_out, ALUresult[13]);
  not not_20 (not_20_out, ALUresult[12]);
  not not_21 (not_21_out, ALUresult[11]);
  not not_22 (not_22_out, ALUresult[10]);
  not not_23 (not_23_out, ALUresult[9]);
  not not_24 (not_24_out, ALUresult[8]);
  not not_25 (not_25_out, ALUresult[7]);
  not not_26 (not_26_out, ALUresult[6]);
  not not_27 (not_27_out, ALUresult[5]);
  not not_28 (not_28_out, ALUresult[4]);
  not not_29 (not_29_out, ALUresult[3]);
  not not_30 (not_30_out, ALUresult[2]);
  not not_31 (not_31_out, ALUresult[1]);
  not not_32 (not_32_out, ALUresult[0]);
endmodule

module imm_gen (
  input  [31:0] Imm_Bits,
  input  [1:0] INST_TYPE,
  output [31:0] Imediato
);

  Multiplexer #(.select(2), .width(32)) multiplexer_1 (
    .in0({{21{Imm_Bits[31]}}, Imm_Bits[30:20]}), .in1({{21{Imm_Bits[31]}}, Imm_Bits[30:25], Imm_Bits[11:7]}),
    .in2({{20{Imm_Bits[31]}}, Imm_Bits[7], Imm_Bits[30:25], Imm_Bits[11:8], 1'b0}), .out(Imediato),
    .sel(INST_TYPE));  // open: in3

  // Other names for the same wires on the sheet: IMM_I[11:0] = Imm_Bits[31:20];
  //   IMM_B[12:1] = {Imm_Bits[31], Imm_Bits[7], Imm_Bits[30:25], Imm_Bits[11:8]};
  //   IMM_S[11:0] = {Imm_Bits[31:25], Imm_Bits[11:7]}; BIT31 = Imm_Bits[31]

  // Notes on the sheet:
  //   - 00 = I
  //   - 01 = S
  //   - 10 = B
  //   INSTRUCTION TYPE
endmodule

module unit_control (
  input  [6:0] OPcode,
  output ALUsrc,
  output MemToReg,
  output RegWrite,
  output MemRead,
  output MemWrite,
  output Branch,
  output ALUop1,
  output ALUop2
);

  wire and_1_out, and_4_out, and_5_out, not_1_out, not_2_out, not_3_out, not_4_out, not_5_out, not_6_out,
       not_7_out, not_8_out, not_9_out, not_11_out, or_1_out;

  and and_1 (and_1_out, OPcode[4], OPcode[5]);
  not not_1 (not_1_out, OPcode[5]);
  not not_2 (not_2_out, OPcode[4]);
  not not_3 (not_3_out, OPcode[6]);
  not not_4 (not_4_out, OPcode[4]);
  not not_5 (not_5_out, OPcode[5]);
  not not_6 (not_6_out, OPcode[6]);
  not not_7 (not_7_out, OPcode[4]);
  not not_8 (not_8_out, and_1_out);
  not not_9 (not_9_out, OPcode[6]);
  not not_10 (MemToReg, OPcode[4]);
  or or_1 (or_1_out, OPcode[4], not_1_out);
  not not_11 (not_11_out, OPcode[6]);
  not not_12 (MemRead, OPcode[5]);
  and and_2 (MemWrite, not_2_out, OPcode[5], not_3_out);
  and and_3 (Branch, not_4_out, OPcode[5], OPcode[6]);
  and and_4 (and_4_out, OPcode[4], not_5_out, not_6_out);
  and and_5 (and_5_out, not_7_out, OPcode[5], OPcode[6]);
  and and_6 (ALUsrc, not_8_out, not_9_out);
  and and_7 (RegWrite, or_1_out, not_11_out);
  or or_2 (ALUop2, and_4_out, and_5_out);

  assign ALUop1 = OPcode[4];

  // Other names for the same wires on the sheet: op4 = OPcode[4]; op5 = OPcode[5]; op6 = OPcode[6]

  // Notes on the sheet:
  //   ALUsrc
  //   MemToReg
  //   RegWrite
  //   MemRead
  //   MemWrite
  //   Branch
  //   ALUop1
  //   ALUop2
endmodule
